# Fritzing sketch wirirng_sketch (saved by Fritzing 0.9.10b)
breadboards: 1

parts:
  WeMos_D1_Mini_Dual_Base_Shield1 = WeMos D1 Mini Dual Base Shield
  U1 = Voltage Regulator [package=to220-adj]
  VCC1 = Battery block 9V
  M1 = DC Motor [voltage_(max)=6V voltage_(min)=3V]
  IC1 = H-Bridge [package=THT]
  C1 = Capacitor Polarized [package=nippon_f80]

nets:
  N1: WeMos_D1_Mini_Dual_Base_Shield1.3V3_Left, U1.OUT
  N2: WeMos_D1_Mini_Dual_Base_Shield1.D5_Left, WeMos_D1_Mini_Dual_Base_Shield1.D5_Right, IC1.1A
  N3: WeMos_D1_Mini_Dual_Base_Shield1.D6_Left, WeMos_D1_Mini_Dual_Base_Shield1.D6_Right, IC1.1Y
  GND: WeMos_D1_Mini_Dual_Base_Shield1.G_Left, WeMos_D1_Mini_Dual_Base_Shield1.G_Right, U1.ADJ, VCC1.-, IC1.GND1, IC1.GND2, IC1.GND3, IC1.GND4, C1.-
  N4: U1.IN, VCC1.+, IC1.1_2EN, IC1.VCC1, C1.+
  N5: M1.pin_1, IC1.4A
  N6: M1.pin_2, IC1.4Y
